# Fritzing sketch weather-pollution (saved by Fritzing 1.0.1rc)
breadboards: 1

parts:
  DHT1 = DHT22 Humidity and Temperature Sensor
  R1 = Resistor [tolerance=±5% power=0.25 resistance=10k package=THT]
  U1 = ESP32-38PinWide [part_number=ESP32-38PinWide]
  U2 = GAS_SENSOR [mpn=fjjhv part_number=fghbkj package=mq-3]
  U3 = GAS_SENSOR [package=mq-3]
  U4 = GAS_SENSOR [package=mq-3]
  LCD2004-I2C1 = LCD2004-I2C
  Grove1 = Grove Dust Sensor
  R2 = Resistor [tolerance=±5% power=0.25 resistance=1000 package=THT]
  R3 = Resistor [tolerance=±5% power=0.25 resistance=1000 package=THT]
  R4 = Resistor [tolerance=±5% power=0.25 resistance=1000 package=THT]

nets:
  N1: DHT1.VDD, DHT1.DATA, R1.Pin_0, U1.3.3, U1.GPIO4, U2.B1, U3.B1, U4.B1
  GND: DHT1.GND, U1.GND, U2.A1, U3.A1, U4.A1, LCD2004-I2C1.GND, Grove1.GND
  N2: U1.GPIO36, R2.Pin_1
  N3: U1.GPIO39, R3.Pin_1
  N4: U1.GPIO34, R4.Pin_1
  N5: U1.GPIO25, Grove1.SIG
  VCC: U1.VIN, LCD2004-I2C1.VCC, Grove1.VCC
  N6: U1.GPIO21, LCD2004-I2C1.SDA
  N7: U1.GPIO22, LCD2004-I2C1.SCL

custom parts:
  ESP32-38PinWide: Generic 38-Pin ESP32 with wide format (only access to one side of pins on a breadboard) based on Stephen Lilley's HiLetgo ESP-WROOM-32 ESP32 ESP-32S Development Board.
  LCD2004-I2C: A standard character display with 4x20 characters. Comes in many colors with LCM2004 IIC attached.
  Grove Dust Sensor: PPD42 Grove Dust Sensor
